# Fritzing sketch wemosd1tft (saved by Fritzing 0.9.3b)

parts:
  WeMos_D1_Mini1 = WeMos D1 Mini
  J1 = Dagu DGServo 9g header (male) [package=THT]
  J2 = Dagu DGServo 9g header (male) [package=THT]
  J3 = Dagu DGServo 9g header (male) [package=THT]
  U1 = Nokia 6100 Color LCD [package=nokia6100_lcd]  # not connected

nets:
  3V3: WeMos_D1_Mini1.3V3, J2.Vcc
  N1: WeMos_D1_Mini1.D0, J1.Vcc
  N2: WeMos_D1_Mini1.D1, J3.Vcc
  N3: WeMos_D1_Mini1.D2, J3.gnd
  N4: WeMos_D1_Mini1.D5, J2.pulse
  N5: WeMos_D1_Mini1.D7, J1.gnd
  N6: WeMos_D1_Mini1.G, J2.gnd

notes:
  GND VCC SCL SDA RES DC CS BL
